# Fritzing sketch dht11_nano (saved by Fritzing 0.9.3b)

parts:
  Composant1 = Arduino Nano (Rev3.0)
  DHT1 = DHT11 Humitidy and Temperature Sensor
  R1 = Resistor [tolerance=±5% resistance=4.7k package=THT]

nets:
  N1: Composant1.D2, DHT1.DATA, R1.Pin_0
  GND: Composant1.GND, DHT1.GND
  5V: Composant1.5V, DHT1.VDD, R1.Pin_1

notes:
  4,7kΩ

custom parts:
  DHT11 Humitidy and Temperature Sensor: DHT11 Humidity and Temperature Sensor
